# Fritzing sketch esquema-projeto (saved by Fritzing 0.9.3b)
breadboards: 1

parts:
  Part1 = Arduino Uno (Rev3) - ICSP
  Part2 = Bluetooth HC-05 Macho
  LCD1 = LCD screen
  KY-1 = Keyes Relay [package=THT]
  LCM1602_IIC1 = LCM1602 IIC [part_number="LCM1602 IIC" chip_label="LCM1602 IIC" package="DIP (Dual Inline) [THT]"]
  Keypad4x1 = Keypad Membran 4x4
  R1 = Resistor [tolerance=±5% resistance=2.2k package=THT]
  R2 = Resistor [tolerance=±5% resistance=2.2k package=THT]
  R3 = Resistor [tolerance=±5% resistance=2.2k package=THT]
  R4 = Resistor [tolerance=±5% resistance=2.2k package=THT]

nets:
  N1: Part1.ICSP_MISO, Part1.D12/MISO, Part2.TXD
  N2: Part1.ICSP_MOSI, Part1.D11_PWM/MOSI, Keypad4x1.Pin8, R4.Pin_1
  GND: Part1.GND, Part2.GND, KY-1.power, LCM1602_IIC1.GND, R1.Pin_0, R2.Pin_0, R3.Pin_0, R4.Pin_0
  N3: Part1.D8, Keypad4x1.Pin5, R1.Pin_1
  N4: Part1.D9_PWM, Keypad4x1.Pin6, R2.Pin_1
  N5: Part1.D10_PWM/SS, Keypad4x1.Pin7, R3.Pin_1
  N6: Part1.D13/SCK, Part2.RXD
  N7: Part1.D0/RX, LCM1602_IIC1.SCL
  N8: Part1.D1/TX, LCM1602_IIC1.SDA
  N9: Part1.D3_PWM, Keypad4x1.Pin1
  N10: Part1.D4, Keypad4x1.Pin2
  N11: Part1.D5_PWM, Keypad4x1.Pin3
  N12: Part1.D6_PWM, Keypad4x1.Pin4
  N13: Part1.D7, KY-1.ground
  VCC: Part1.5V, Part2.VCC, KY-1.signal, LCM1602_IIC1.VCC
  VSS: LCD1.VSS, LCM1602_IIC1.VSS
  VDD: LCD1.VDD, LCM1602_IIC1.VDD
  N14: LCD1.V0, LCM1602_IIC1.V0
  N15: LCD1.RS, LCM1602_IIC1.RS
  N16: LCD1.R/W, LCM1602_IIC1.RW
  N17: LCD1.E, LCM1602_IIC1.E
  N18: LCD1.DB0, LCM1602_IIC1.D0
  N19: LCD1.DB1, LCM1602_IIC1.D1
  N20: LCD1.DB2, LCM1602_IIC1.D2
  N21: LCD1.DB3, LCM1602_IIC1.D3
  N22: LCD1.DB4, LCM1602_IIC1.D4
  N23: LCD1.DB5, LCM1602_IIC1.D5
  N24: LCD1.DB6, LCM1602_IIC1.D6
  N25: LCD1.DB7, LCM1602_IIC1.D7
  N26: LCD1.LED+, LCM1602_IIC1.A
  N27: LCD1.LED-, LCM1602_IIC1.K
  N28: LCM1602_IIC1.LED_A, LCM1602_IIC1.LED_B

custom parts:
  Keyes Relay: The Keyes 5V relay module is suitable for SCM development, home appliance control. It uses a 5V~12V TIL control signal which can control DC / AC signal.
  LCM1602 IIC: I2C-Module to use a 1602 or 2004 LCD on with the wire.h libory Serial LCD Modul
  Keypad Membran 4x4: Membrane Keypad 4x4 Matrix
